// Digital circuit 12-16.dig as structural Verilog
module _12_16 (
  input  Z_Flag,
  input  N_Flag,
  input  C_Flag,
  input  V_Flag,
  input  Z_Bit,
  input  [2:0] RS1,
  input  [2:0] RS2,
  output READFLAG_ENABLE,
  output [15:0] FL,
  output cond
);

  wire and_5_out, comparator_1_eq, comparator_2_eq, not_1_out;

  Comparator #(.Bits(3)) comparator_1 (.a(RS1), .b(3'b111), .eq(comparator_1_eq));  // open: gt, lt
  Comparator #(.Bits(3)) comparator_2 (.a(RS2), .b(3'b111), .eq(comparator_2_eq));  // open: gt, lt
  or or_1 (READFLAG_ENABLE, comparator_1_eq, comparator_2_eq);
  and and_1 (FL[2], V_Flag, READFLAG_ENABLE);
  and and_2 (FL[3], C_Flag, READFLAG_ENABLE);
  and and_3 (FL[1], N_Flag, READFLAG_ENABLE);
  and and_4 (FL[0], Z_Flag, READFLAG_ENABLE);
  not not_1 (not_1_out, Z_Bit);
  and and_5 (and_5_out, Z_Bit, Z_Flag);
  or or_2 (cond, not_1_out, and_5_out);

  assign FL[15:4] = {12{1'b0}};
endmodule
