// Digital circuit 16bitter.dig as structural Verilog
module _16bitter (
  input  [15:0] A,
  input  [15:0] B,
  input  SUB,
  output [15:0] Q,
  output C_out,
  output V
);

  wire add_1_c_o, add_2_c_o, add_3_c_o, add_4_c_o, add_5_c_o, xor_4_out, xor_5_out, xor_6_out, xor_7_out;
  wire [3:0] xor_1_out, xor_2_out, xor_3_out;

  assign xor_1_out = B[3:0] ^ {4{SUB}};  // XOr xor_1, 4 bits wide
  assign xor_2_out = B[7:4] ^ {4{SUB}};  // XOr xor_2, 4 bits wide
  assign xor_3_out = B[11:8] ^ {4{SUB}};  // XOr xor_3, 4 bits wide
  xor xor_4 (xor_4_out, B[12], SUB);
  xor xor_5 (xor_5_out, B[13], SUB);
  xor xor_6 (xor_6_out, B[14], SUB);
  xor xor_7 (xor_7_out, B[15], SUB);
  Add #(.Bits(4)) add_1 (.a(A[3:0]), .b(xor_1_out), .c_i(SUB), .s(Q[3:0]), .c_o(add_1_c_o));
  Add #(.Bits(4)) add_2 (.a(A[7:4]), .b(xor_2_out), .c_i(add_1_c_o), .s(Q[7:4]), .c_o(add_2_c_o));
  Add #(.Bits(4)) add_3 (.a(A[11:8]), .b(xor_3_out), .c_i(add_2_c_o), .s(Q[11:8]), .c_o(add_3_c_o));
  Add add_4 (.a(A[12]), .b(xor_4_out), .c_i(add_3_c_o), .s(Q[12]), .c_o(add_4_c_o));
  Add add_5 (.a(A[13]), .b(xor_5_out), .c_i(add_4_c_o), .s(Q[13]), .c_o(add_5_c_o));
  Add add_6 (.a(A[14]), .b(xor_6_out), .c_i(add_5_c_o), .s(Q[14]), .c_o(V));
  Add add_7 (.a(A[15]), .b(xor_7_out), .c_i(V), .s(Q[15]), .c_o(C_out));

  // Notes on the sheet:
  //   A: First adder input
  //   B: Second adder input
  //   SUB: Selection bit to enable subtract mode.
  //   If set high, the unit should perform a subtraction.
  //   Q: Result of adding A and B
endmodule
