// Digital circuit AddSub16bit.dig as structural Verilog
module AddSub16bit (
  input  ALUSEL,
  input  [15:0] A,
  input  [15:0] B,
  output [15:0] Addition,
  output [15:0] Subtraction,
  output c_out,
  output C_in_14,
  output [15:0] Q
);

  wire not_1_out;

  not not_1 (not_1_out, ALUSEL);
  _16bitter _16bitter_1 (.A(A), .B(B), .SUB(ALUSEL), .Q(Q), .C_out(c_out), .V(C_in_14));
  and and_1 (Addition[0], Q[0], not_1_out);
  and and_2 (Addition[1], Q[1], not_1_out);
  and and_3 (Addition[2], Q[2], not_1_out);
  and and_4 (Addition[3], Q[3], not_1_out);
  and and_5 (Addition[4], Q[4], not_1_out);
  and and_6 (Addition[5], Q[5], not_1_out);
  and and_7 (Addition[6], Q[6], not_1_out);
  and and_8 (Addition[7], Q[7], not_1_out);
  and and_9 (Addition[8], Q[8], not_1_out);
  and and_10 (Addition[9], Q[9], not_1_out);
  and and_11 (Addition[10], Q[10], not_1_out);
  and and_12 (Addition[11], Q[11], not_1_out);
  and and_13 (Addition[12], Q[12], not_1_out);
  and and_14 (Addition[13], Q[13], not_1_out);
  and and_15 (Addition[14], Q[14], not_1_out);
  and and_16 (Addition[15], Q[15], not_1_out);
  and and_17 (Subtraction[0], Q[0], ALUSEL);
  and and_18 (Subtraction[1], Q[1], ALUSEL);
  and and_19 (Subtraction[2], Q[2], ALUSEL);
  and and_20 (Subtraction[3], Q[3], ALUSEL);
  and and_21 (Subtraction[4], Q[4], ALUSEL);
  and and_22 (Subtraction[5], Q[5], ALUSEL);
  and and_23 (Subtraction[6], Q[6], ALUSEL);
  and and_24 (Subtraction[7], Q[7], ALUSEL);
  and and_25 (Subtraction[8], Q[8], ALUSEL);
  and and_26 (Subtraction[9], Q[9], ALUSEL);
  and and_27 (Subtraction[10], Q[10], ALUSEL);
  and and_28 (Subtraction[11], Q[11], ALUSEL);
  and and_29 (Subtraction[12], Q[12], ALUSEL);
  and and_30 (Subtraction[13], Q[13], ALUSEL);
  and and_31 (Subtraction[14], Q[14], ALUSEL);
  and and_32 (Subtraction[15], Q[15], ALUSEL);
endmodule
