// Digital circuit Comparators.dig as structural Verilog
module Comparators (
  input  [3:0] opcode,
  output ADD,
  output ORR,
  output MOV,
  output SUB,
  output SETH,
  output MOVL,
  output AND,
  output BX,
  output BL,
  output B,
  output STR,
  output LDR
);

  Comparator #(.Bits(4)) is_movl (.a(opcode), .b(4'b0000), .eq(MOVL));  // open: gt, lt
  Comparator #(.Bits(4)) is_add (.a(opcode), .b(4'b0001), .eq(ADD));  // open: gt, lt
  Comparator #(.Bits(4)) is_ldr (.a(opcode), .b(4'b0010), .eq(LDR));  // open: gt, lt
  Comparator #(.Bits(4)) is_str (.a(opcode), .b(4'b0011), .eq(STR));  // open: gt, lt
  Comparator #(.Bits(4)) is_sub (.a(opcode), .b(4'b0100), .eq(SUB));  // open: gt, lt
  Comparator #(.Bits(4)) is_and (.a(opcode), .b(4'b0101), .eq(AND));  // open: gt, lt
  Comparator #(.Bits(4)) is_orr (.a(opcode), .b(4'b0110), .eq(ORR));  // open: gt, lt
  Comparator #(.Bits(4)) is_mov (.a(opcode), .b(4'b0111), .eq(MOV));  // open: gt, lt
  Comparator #(.Bits(4)) is_seth (.a(opcode), .b(4'b1000), .eq(SETH));  // open: gt, lt
  Comparator #(.Bits(4)) is_bx (.a(opcode), .b(4'b1001), .eq(BX));  // open: gt, lt
  Comparator #(.Bits(4)) is_bl (.a(opcode), .b(4'b1010), .eq(BL));  // open: gt, lt
  Comparator #(.Bits(4)) is_b (.a(opcode), .b(4'b1011), .eq(B));  // open: gt, lt
endmodule
