// Digital circuit MYALU.dig as structural Verilog
module MYALU (
  input  [15:0] A,
  input  [15:0] B,
  input  [1:0] ALUOP,
  output [15:0] RESULT,
  output [3:0] FLAG
);

  wire addsub16bit_1_c_out, and_2_out, v_flag_1_v;
  wire [15:0] addsub16bit_1_addition, addsub16bit_1_q, addsub16bit_1_subtraction, and_1_out, or_1_out;

  AddSub16bit addsub16bit_1 (
    .ALUSEL(and_2_out), .A(A), .B(B), .Addition(addsub16bit_1_addition),
    .Subtraction(addsub16bit_1_subtraction), .c_out(addsub16bit_1_c_out), .Q(addsub16bit_1_q));  // open: C_in_14
  assign and_1_out = A & B;  // And and_1, 16 bits wide
  assign or_1_out = A | B;  // Or or_1, 16 bits wide
  V_FLAG v_flag_1 (.A(A), .B(B), .Q(addsub16bit_1_q), .SUB(and_2_out), .V(v_flag_1_v));
  and and_2 (and_2_out, ALUOP[1], ALUOP[0]);
  Multiplexer #(.Selector_Bits(2), .Bits(16)) multiplexer_1 (
    .sel(ALUOP), .in_0(and_1_out), .in_1(or_1_out), .in_2(addsub16bit_1_addition),
    .in_3(addsub16bit_1_subtraction), .out({FLAG[1], RESULT[14:0]}));
  Multiplexer #(.Selector_Bits(2)) multiplexer_2 (
    .sel(ALUOP), .in_0(1'b0), .in_1(1'b0), .in_2(addsub16bit_1_c_out), .in_3(addsub16bit_1_c_out),
    .out(FLAG[3]));
  Multiplexer #(.Selector_Bits(2)) multiplexer_3 (
    .sel(ALUOP), .in_0(1'b0), .in_1(1'b0), .in_2(v_flag_1_v), .in_3(v_flag_1_v), .out(FLAG[2]));
  nor nor_1 (FLAG[0], RESULT[0], RESULT[1], RESULT[2], RESULT[3], RESULT[4], RESULT[5], RESULT[6], RESULT[7], RESULT[8], RESULT[9], RESULT[10], RESULT[11], RESULT[12], RESULT[13], RESULT[14], FLAG[1]);

  assign RESULT[15] = FLAG[1];

  // Notes on the sheet:
  //   A: First input to ALU
  //   B: Second input to ALU
  //   ALUOP: Operation selection input
  //   RESULT: The result of this ALU operation
  //   FLAG: The flags associated with the result of this ALU operation
  //   0. Z (zero)
  //   1. N (negative)
  //   2. C (carry)
  //   3. V (overflow)
endmodule

/* Test case RESULT:
ALUOP A B RESULT

# Test small results
loop(a, 1 << 4)
loop(b, 1 << 4)
    (00) (a) (b) (a & b)
    (01) (a) (b) (a | b)
    (10) (a) (b) ((a + b) & 0xFFFF)
    (11) (a) (b) ((a - b) & 0xFFFF)
end loop
end loop


# Test large results
loop(i, 1000)
    let a = random(1 << 16);
    let b = random(1 << 16);

    (00) (a) (b) (a & b)
    (01) (a) (b) (a | b)
    (10) (a) (b) ((a + b) & 0xFFFF)
    (11) (a) (b) ((a - b) & 0xFFFF)
end loop
*/

/* Test case Z:
ALUOP A B Z

declare Z = FLAG & 0b1;

# Test all zero cases
00 0 0 1
01 0 0 1
10 0 0 1
11 0 0 1

# Test 1 + (-1) = 0
10 1 0xFFFF 1

# Test with a single bit set in A
loop(s, 16)
    let a = 1 << s;

    00 (a) 0 1
    01 (a) 0 (a = 0)
    10 (a) 0 (a = 0)
    11 (a) 0 (a = 0)
end loop

# Test random inputs
loop(i, 200)
    let a = random(1 << 16);
    let b = random(1 << 16);

    00 (a) (b) ((a & b) = 0)
    01 (a) (b) ((a | b) = 0)
    10 (a) (b) (((a + b) & 0xFFFF) = 0)
    11 (a) (b) (((a - b) & 0xFFFF) = 0)
end loop
*/

/* Test case N:
ALUOP A B N

declare N = (FLAG >> 1) & 0b1;

# Test all zero cases
0b00 0 0 0
0b01 0 0 0
0b10 0 0 0
0b11 0 0 0

0b00 1 0xFFFF 0

# Test with a single bit set in A
loop(s, 16)
    let a = 1 << s;

    0b00 (a) 0 0
    0b01 (a) 0 ((a >> 15) & 0b1)
    0b10 (a) 0 ((a >> 15) & 0b1)
    0b11 (a) 0 ((a >> 15) & 0b1)
end loop

# Test random inputs
loop(i, 200)
    let a = random(1 << 16);
    let b = random(1 << 16);

    0b00 (a) (b) (((a & b) >> 15) & 0b1)
    0b01 (a) (b) (((a | b) >> 15) & 0b1)
    0b10 (a) (b) (((a + b) >> 15) & 0b1)
    0b11 (a) (b) (((a - b) >> 15) & 0b1)
end loop
*/

/* Test case C:
ALUOP A B C

declare C = (FLAG >> 3) & 0b1;

0b10 0 0 0

# (0 - 0) is implemented as 0 + (0xFFFF + 1), so a carry is expected
0b11 0 0 1

# Carry should propagate all the way from the first bit if necessary
0b10 1 0xFFFF 1

# Test with a single bit set in A
loop(s, 16)
    let a = 1 << s;

    0b00 (a) 0 0  # carry is defined as 0 for AND
    0b01 (a) 0 0  # carry is defined as 0 for OR
    0b10 (a) 0 0
    0b11 (a) 0 1  # (a - 0) is implemented as (a + 0xFFFF + 1) in the adder, so a carry is always expected
end loop

# Adding 15 bit values should never carry
loop(i, 100)
    0b10 (random(1 << 15)) (random(1 << 15)) 0
end loop

# Test random inputs
loop(i, 200)
    let a = random(1 << 16);
    let b = random(1 << 16);

    0b10 (a) (b) (((a + b) >> 16) & 0b1)
    0b11 (a) (b) (~((a - b) >> 16) & 0b1)
end loop

# AND and OR never set carry
loop(i, 100)
    let a = random(1 << 16);
    let b = random(1 << 16);
    0b00 (a) (b) 0
    0b01 (a) (b) 0
end loop
*/

/* Test case V:
ALUOP A B V

declare V = (FLAG >> 2) & 0b1;

0b10 0 0 0
0b11 0 0 0

# 1 + (-1) = 0  ; different input signs = no overflow here!
0b10 1 0xFFFF 0

# 3 - 5 = 3 + (-5) = -2  ; subtraction inverts the second operand sign
0b11 3 5 0

# Some edge cases when subtracting 0x8000
0b11 0x8000 0x8000 0
0b11 0xFFFF 0x8000 0
0b11 0x7FFF 0x8000 1

# Test with a single bit set in A
loop(s, 16)
    let a = 1 << s;

    0b00 (a) 0 0  # overflow is defined as 0 for AND
    0b10 (a) 0 0  # overflow is defined as 0 for OR
    0b10 (a) 0 0
    0b11 (a) 0 0
end loop

# Test random inputs
loop(i, 200)
    let a = random(1 << 16);
    let b = random(1 << 16);

    0b10 (a) (b) (((~(a ^ b) & (a ^ (a + b))) >> 15) & 0b1)
    0b11 (a) (b) (((~(a ^ -b) & (a ^ (a - b))) >> 15) & 0b1)
end loop

# AND and OR never set overflow
loop(i, 100)
    let a = random(1 << 16);
    let b = random(1 << 16);
    0b00 (a) (b) 0
    0b01 (a) (b) 0
end loop
*/
