// Digital circuit V FLAG.dig as structural Verilog
module V_FLAG (
  input  [15:0] A,
  input  [15:0] B,
  input  [15:0] Q,
  input  SUB,
  output V
);

  wire and_1_out, and_2_out, and_3_out, and_4_out, and_5_out, and_6_out, not_1_out, not_2_out, not_3_out,
       not_4_out, not_5_out, not_6_out, not_7_out, or_1_out, or_3_out;

  not not_1 (not_1_out, Q[15]);
  and and_1 (and_1_out, not_1_out, B[15], A[15]);
  not not_2 (not_2_out, A[15]);
  not not_3 (not_3_out, B[15]);
  and and_2 (and_2_out, Q[15], not_3_out, not_2_out);
  or or_1 (or_1_out, and_2_out, and_1_out);
  not not_4 (not_4_out, SUB);
  and and_3 (and_3_out, not_4_out, or_1_out);
  or or_2 (V, and_5_out, and_3_out);
  not not_5 (not_5_out, B[15]);
  not not_6 (not_6_out, Q[15]);
  and and_4 (and_4_out, not_6_out, not_5_out, A[15]);
  and and_5 (and_5_out, SUB, or_3_out);
  not not_7 (not_7_out, A[15]);
  and and_6 (and_6_out, Q[15], B[15], not_7_out);
  or or_3 (or_3_out, and_6_out, and_4_out);
endmodule
