// Digital circuit WorkingOut.dig as structural Verilog
module WorkingOut (
  input  [15:0] _2D,
  input  Z_Flag,
  output [2:0] WS,
  output [2:0] RS5,
  output [2:0] RS6,
  output WE,
  output FLEN,
  output [1:0] ALUOP,
  output STR,
  output LDR,
  output [1:0] DMUX,
  output COND
);

  wire and_1_out, comparator_1_eq, comparator_2_eq, comparator_2_gt, comparator_3_eq, comparator_3_lt,
       MOVL_eq, multiplexer_3_out, or_1_out, or_4_out, or_5_out, or_6_out;

  Multiplexer multiplexer_1 (.sel(_2D[11]), .in_0(1'b1), .in_1(Z_Flag), .out(COND));
  Multiplexer #(.Bits(3)) multiplexer_2 (.sel(comparator_1_eq), .in_0(_2D[2:0]), .in_1(_2D[10:8]), .out(RS6));
  Comparator #(.Bits(4)) comparator_1 (.a(_2D[15:12]), .b(4'b0111), .eq(comparator_1_eq));  // open: gt, lt
  Comparator #(.Bits(4)) MOVL (.a(_2D[15:12]), .b(4'b0000), .eq(MOVL_eq));  // open: gt, lt
  Comparator #(.Bits(2)) comparator_2 (
    .a(_2D[13:12]), .b(2'b00), .gt(comparator_2_gt), .eq(comparator_2_eq));  // open: lt
  Comparator #(.Bits(2)) comparator_3 (
    .a(_2D[13:12]), .b(2'b11), .eq(comparator_3_eq), .lt(comparator_3_lt));  // open: gt
  or or_1 (or_1_out, _2D[12], _2D[15], _2D[13]);
  or or_2 (DMUX[0], MOVL_eq, or_1_out);
  or or_3 (DMUX[1], MOVL_eq, _2D[14]);
  or or_4 (or_4_out, comparator_2_gt, comparator_2_eq);
  or or_5 (or_5_out, comparator_3_eq, comparator_3_lt);
  or or_6 (or_6_out, DMUX[0], DMUX[1]);
  and and_1 (and_1_out, or_4_out, or_5_out);
  Multiplexer multiplexer_3 (.sel(comparator_1_eq), .in_0(or_6_out), .in_1(1'b0), .out(multiplexer_3_out));
  and and_2 (STR, COND, comparator_1_eq);
  and and_3 (WE, COND, multiplexer_3_out);
  and and_4 (FLEN, COND, and_1_out);

  assign ALUOP = _2D[13:12];
  assign LDR = _2D[14];
  assign RS5 = _2D[6:4];
  assign WS = _2D[10:8];

  // Notes on the sheet:
  //   Z
  //   Rd
  //   Ra
  //   Rb
  //   opcode
endmodule
