// Digital circuit X.reg_file_complete.dig as structural Verilog
module X_reg_file_complete (
  input  [2:0] RS1,
  input  [2:0] RS2,
  input  [2:0] WS,
  input  WE,
  input  [15:0] IN,
  input  clk,
  output [15:0] OUT1,
  output [15:0] OUT2
);

  Decoder #(.Bits(3)) WS_DEC ();  // open: sel, out_0, out_1
  Register #(.Bits(16)) R1 ();  // open: D, C, en, Q
  Register #(.Bits(16)) R2 ();  // open: D, C, en, Q
  Register #(.Bits(16)) R3 ();  // open: D, C, en, Q
  Register #(.Bits(16)) R4 ();  // open: D, C, en, Q
  Multiplexer #(.Bits(16)) MUX1 (.in_0({16{1'b0}}), .out(OUT1));  // open: sel, in_1
  Multiplexer #(.Bits(16)) MUX2 (.in_0({16{1'b0}}), .out(OUT2));  // open: sel, in_1

  // Notes on the sheet:
  //   RS1: The index of the register which should output its value to OUT1.
  //   RS2: The index of the register which should output its value to OUT2.
  //   WS: The index of the register which should save the value on IN on the next clock cycle (if WE is high).
  //   WE: Whether the register selected by WS should save the value from IN on the next cycle.
  //   IN: The value to be saved into the register specified by WS if WE is high,
  //   OUT1: The value in the register specified by RS1.
  //   OUT2: The value in the register specified by RS2.
endmodule

/* Test case:
clk RS1 RS2 WS WE IN OUT1 OUT2
c 0 0 0 1 0x1234 0x0000 0x0000
c 1 0 1 1 0xBEEF 0xBEEF 0x0000
c 2 1 2 1 0xDEAD 0xDEAD 0xBEEF
c 3 2 3 1 0xFFFF 0xFFFF 0xDEAD
c 3 2 3 0 0xABCD 0xFFFF 0xDEAD
c 3 2 2 0 0xABCD 0xFFFF 0xDEAD
c 1 0 1 0 0xABCD 0xBEEF 0x0000
c 1 0 0 0 0xABCD 0xBEEF 0x0000
c 1 0 2 1 0xBADE 0xBEEF 0x0000
c 0 2 2 1 0xBADE 0x0000 0xBADE
c 0 0 2 0 0x1234 0x0000 0x0000
c 2 3 0 1 0x0000 0xBADE 0xFFFF
c 0 0 2 0 0x1234 0x0000 0x0000
*/
