// Digital circuit control_unit.dig as structural Verilog
module control_unit (
  input  [15:0] _2D,
  input  Z_Flag,
  output [2:0] WS,
  output [2:0] RS1,
  output [2:0] RS2,
  output WE,
  output FLEN,
  output [1:0] ALUOP,
  output STR,
  output LDR,
  output [1:0] DMUX,
  output COND
);

  wire and_1_out, comparator_1_eq, comparator_2_eq, comparator_2_gt, comparator_3_eq, comparator_3_lt,
       MOVL_eq, multiplexer_3_out, or_1_out, or_4_out, or_5_out, or_6_out;

  Comparator #(.Bits(4)) comparator_1 (.a(_2D[15:12]), .b(4'b0111), .eq(comparator_1_eq));  // open: gt, lt
  Comparator #(.Bits(4)) MOVL (.a(_2D[15:12]), .b(4'b0000), .eq(MOVL_eq));  // open: gt, lt
  Comparator #(.Bits(2)) comparator_2 (
    .a(_2D[13:12]), .b(2'b00), .gt(comparator_2_gt), .eq(comparator_2_eq));  // open: lt
  Comparator #(.Bits(2)) comparator_3 (
    .a(_2D[13:12]), .b(2'b11), .eq(comparator_3_eq), .lt(comparator_3_lt));  // open: gt
  or or_1 (or_1_out, _2D[12], _2D[15], _2D[13]);
  Multiplexer multiplexer_1 (.sel(_2D[11]), .in_0(1'b1), .in_1(Z_Flag), .out(COND));
  Multiplexer #(.Bits(3)) multiplexer_2 (.sel(comparator_1_eq), .in_0(_2D[2:0]), .in_1(_2D[10:8]), .out(RS2));
  or or_2 (DMUX[0], MOVL_eq, or_1_out);
  or or_3 (DMUX[1], MOVL_eq, _2D[14]);
  or or_4 (or_4_out, comparator_2_gt, comparator_2_eq);
  or or_5 (or_5_out, comparator_3_eq, comparator_3_lt);
  or or_6 (or_6_out, DMUX[0], DMUX[1]);
  and and_1 (and_1_out, or_4_out, or_5_out);
  Multiplexer multiplexer_3 (.sel(comparator_1_eq), .in_0(or_6_out), .in_1(1'b0), .out(multiplexer_3_out));
  and and_2 (STR, COND, comparator_1_eq);
  and and_3 (WE, COND, multiplexer_3_out);
  and and_4 (FLEN, COND, and_1_out);

  assign ALUOP = _2D[13:12];
  assign LDR = _2D[14];
  assign RS1 = _2D[6:4];
  assign WS = _2D[10:8];

  // Notes on the sheet:
  //   opcode
  //   Z
  //   Rb
  //   Rd
  //   Ra
endmodule

/* Test case All Tests:
	2D                                    WE  ALUOP  RS1   RS2  WS  STR  LDR DMUX

let aluop  = 0b1000;
let ldrop  = 0b0100;
let strop  = 0b0111;
let movlop = 0b0000;

loop(rd, 1<<3)
loop(ra, 1<<3)
loop(rb, 1<<3)

loop(i, 4)
	((aluop+i)<<12 | rd<<8 | ra<<4 | rb<<0) 1  (i)     (ra)  (rb) (rd)  0   X    1  #test add/sub/and/orr
end loop

	(ldrop    <<12 | rd<<8 | ra<<4 )        1  X       (ra)  x    (rd)  0   1    2  #test ldr
	(strop    <<12 | rd<<8 | ra<<4 )        0  X       (ra)  (rd)  X    1   X    X  #test str
	
	let imm = random(256);
	(movlop   <<12 | rd<<8 | imm )          1  X       X      X   (rd)  0   X    3  #test movl

end loop
end loop
end loop
*/

/* Test case WS:
	2D                                    WS 

let aluop  = 0b1000;
let ldrop  = 0b0100;
let strop  = 0b0111;
let movlop = 0b0000;

loop(rd, 1<<3)
loop(ra, 1<<3)
loop(rb, 1<<3)

loop(i, 4)
	((aluop+i)<<12 | rd<<8 | ra<<4 | rb<<0) (rd)  #test add/sub/and/orr
end loop

	(ldrop    <<12 | rd<<8 | ra<<4 )        (rd)   #test ldr
	(strop    <<12 | rd<<8 | ra<<4 )        X     #test str
	
	let imm = random(256);
	(movlop   <<12 | rd<<8 | imm )          (rd)  #test movl

end loop
end loop
end loop
*/

/* Test case RS1:
	2D                                    RS1  

let aluop  = 0b1000;
let ldrop  = 0b0100;
let strop  = 0b0111;
let movlop = 0b0000;

loop(rd, 1<<3)
loop(ra, 1<<3)
loop(rb, 1<<3)

loop(i, 4)
	((aluop+i)<<12 | rd<<8 | ra<<4 | rb<<0) (ra)  #test add/sub/and/orr
end loop

	(ldrop    <<12 | rd<<8 | ra<<4 )        (ra)  #test ldr
	(strop    <<12 | rd<<8 | ra<<4 )        (ra)  #test str

end loop
end loop
end loop
*/

/* Test case RS2:
	2D                                    RS2  

let aluop  = 0b1000;
let ldrop  = 0b0100;
let strop  = 0b0111;
let movlop = 0b0000;

loop(rd, 1<<3)
loop(ra, 1<<3)
loop(rb, 1<<3)

loop(i, 4)
	((aluop+i)<<12 | rd<<8 | ra<<4 | rb<<0) (rb) #test add/sub/and/orr
end loop
	(strop    <<12 | rd<<8 | ra<<4 )        (rd) #test str

end loop
end loop
end loop
*/

/* Test case STR:
	2D                                    STR 

let aluop  = 0b1000;
let ldrop  = 0b0100;
let strop  = 0b0111;
let movlop = 0b0000;

loop(rd, 1<<3)
loop(ra, 1<<3)
loop(rb, 1<<3)

loop(i, 4)
	((aluop+i)<<12 | rd<<8 | ra<<4 | rb<<0) 0  #test add/sub/and/orr
end loop

	(ldrop    <<12 | rd<<8 | ra<<4 )        0  #test ldr
	(strop    <<12 | rd<<8 | ra<<4 )        1  #test str
	
	let imm = random(256);
	(movlop   <<12 | rd<<8 | imm )          0  #test movl

end loop
end loop
end loop
*/

/* Test case WE:
	2D                                    WE  

let aluop  = 0b1000;
let ldrop  = 0b0100;
let strop  = 0b0111;
let movlop = 0b0000;

loop(rd, 1<<3)
loop(ra, 1<<3)
loop(rb, 1<<3)

loop(i, 4)
	((aluop+i)<<12 | rd<<8 | ra<<4 | rb<<0) 1  #test add/sub/and/orr
end loop

	(ldrop    <<12 | rd<<8 | ra<<4 )        1  #test ldr
	(strop    <<12 | rd<<8 | ra<<4 )        0  #test str
	
	let imm = random(256);
	(movlop   <<12 | rd<<8 | imm )          1  #test movl

end loop
end loop
end loop
*/

/* Test case LDR:
	2D                                    LDR 

let aluop  = 0b1000;
let ldrop  = 0b0100;
let strop  = 0b0111;
let movlop = 0b0000;

loop(rd, 1<<3)
loop(ra, 1<<3)
loop(rb, 1<<3)

loop(i, 4)
	((aluop+i)<<12 | rd<<8 | ra<<4 | rb<<0) X    #test add/sub/and/orr
end loop

	(ldrop    <<12 | rd<<8 | ra<<4 )        1    #test ldr
	(strop    <<12 | rd<<8 | ra<<4 )        X    #test str
	
	let imm = random(256);
	(movlop   <<12 | rd<<8 | imm )          X    #test movl

end loop
end loop
end loop
*/

/* Test case DMUX:
	2D                                    DMUX

let aluop  = 0b1000;
let ldrop  = 0b0100;
let strop  = 0b0111;
let movlop = 0b0000;

loop(rd, 1<<3)
loop(ra, 1<<3)
loop(rb, 1<<3)

loop(i, 4)
	((aluop+i)<<12 | rd<<8 | ra<<4 | rb<<0) 1  #test add/sub/and/orr
end loop

	(ldrop    <<12 | rd<<8 | ra<<4 )        2  #test ldr
	
	let imm = random(256);
	(movlop   <<12 | rd<<8 | imm )          3  #test movl

end loop
end loop
end loop
*/

/* Test case ALUOP:
	2D                                    ALUOP 

let aluop  = 0b1000;
let ldrop  = 0b0100;
let strop  = 0b0111;
let movlop = 0b0000;

loop(rd, 1<<3)
loop(ra, 1<<3)
loop(rb, 1<<3)

loop(i, 4)
	((aluop+i)<<12 | rd<<8 | ra<<4 | rb<<0) (i)    #test add/sub/and/orr
end loop

end loop
end loop
end loop
*/
