// Digital circuit cpu.dig as structural Verilog
module cpu (
  input  CLK,
  input  [2:0] RS1,
  input  [2:0] RS2,
  input  [2:0] WS,
  input  STR,
  input  LDR,
  input  WE,
  input  [1:0] ALUOP,
  input  [1:0] DMUX,
  output Z,
  output N,
  output C,
  output V
);

  wire [15:0] multiplexer_1_out, myalu_1_result, notconnected_1_out, PC_q, plus_1_s, RAM_d1, RAM_d2,
       reg_file_1_out1, reg_file_1_out2;

  Register #(.Bits(16), .isProgramCounter("true")) PC (.D(plus_1_s), .C(CLK), .en(1'b1), .Q(PC_q));
  Add #(.Bits(16)) plus_1 (.a(16'h1), .b(PC_q), .c_i(1'b0), .s(plus_1_s));  // open: c_o
  RAMDualAccess #(.AddrBits(16), .Bits(16)) RAM (
    .str(STR), .C(CLK), .ld(LDR), .A1(reg_file_1_out1), .Din1(reg_file_1_out2), .A2(PC_q), .D1(RAM_d1),
    .D2(RAM_d2));
  Multiplexer #(.Selector_Bits(2), .Bits(16)) multiplexer_1 (
    .sel(DMUX), .in_0(notconnected_1_out), .in_1(myalu_1_result), .in_2(RAM_d1),
    .in_3({{8{1'b0}}, RAM_d2[7:0]}), .out(multiplexer_1_out));
  // NotConnected on notconnected_1_out
  // Probe DATA on multiplexer_1_out
  reg_file reg_file_1 (
    .WS(RS1), .RS1(RS2), .RS2(WS), .WE(WE), .IN(multiplexer_1_out), .clk(CLK), .OUT1(reg_file_1_out1),
    .OUT2(reg_file_1_out2));  // open: _16FLAG, FLEN, PC
  MYALU myalu_1 (.A(reg_file_1_out1), .B(reg_file_1_out2), .ALUOP(ALUOP), .RESULT(myalu_1_result), .FLAG({V, C, N, Z}));
  // Pins of 8 and 18 bits meet at {18{1'b0}}
endmodule

/* Test case Manual CPU:
# Testing the manual CPU
# CLK: Clock
# ALUOP: ALU opcode
#    00 - AND, 01 - ORR, 10 - ADD, 11 - SUB
# RS1: First operand
# RS2: Second operand
# WS: Destination register to write to
# WE: (Register) Write enable
# STR: Store
# LDR: Load
# R1-R4: Registers
# DATA: Output from Data Multiplexer
#  01 - ALU, 10 - MEMORY, 11-INPUT, 00-X
# IN: Manual data input
CLK ALUOP RS1 RS2 WS WE STR LDR IN DMUX    R1 R2 R3     R4     DATA

0   0     0   0   0  0  0   0   0  x       x  x  x      x      x      # registers uninitalised
C   x     x   x   1  1  0   0   1  3       1  x  x      x      1      # R1 := 1
C   x     x   x   2  1  0   0   2  3       1  2  x      x      2      # R2 := 2
C   x     0   x   3  1  0   1   0  2       1  2  0xAAAA x      0xAAAA # R3 := mem[RZ]
C   x     1   x   4  1  0   1   0  2       1  2  0xAAAA 0xBBBB 0xBBBB # R4 := mem[R1]
C   2     3   4   4  1  0   0   0  1       1  2  0xAAAA 0x6665 x      # R4 := R4 + R3
C   x     2   4   x  0  1   0   0  x       1  2  0xAAAA 0x6665 x      # mem[R2] := R4
C   x     2   x   x  0  0   1   0  2       1  2  0xAAAA 0x6665 0x6665 # check mem[R2] := R4

program(0xAAAA, 0xBBBB, 0xCCCC, 0xDDDD)
*/
