// Digital circuit ex2.dig as structural Verilog
module ex2 (
  input  [15:0] A,
  input  [15:0] B,
  input  [2:0] ALUOP,
  output [15:0] RESULT,
  output [3:0] FLAG
);

  wire addsub16bit_1_c_in_14, addsub16bit_1_c_out, xor_2_out;
  wire [15:0] addsub16bit_1_addition, addsub16bit_1_subtraction, and_1_out, nand_1_out, nor_1_out, not_1_out,
       or_1_out, xor_1_out;

  assign nand_1_out = ~(A & B);  // NAnd nand_1, 16 bits wide
  assign nor_1_out = ~(A | B);  // NOr nor_1, 16 bits wide
  assign and_1_out = A & B;  // And and_1, 16 bits wide
  assign or_1_out = A | B;  // Or or_1, 16 bits wide
  assign xor_1_out = A ^ B;  // XOr xor_1, 16 bits wide
  assign not_1_out = ~A;  // Not not_1, 16 bits wide
  AddSub16bit addsub16bit_1 (
    .ALUSEL(ALUOP[0]), .A(A), .B(B), .Addition(addsub16bit_1_addition),
    .Subtraction(addsub16bit_1_subtraction), .c_out(addsub16bit_1_c_out), .C_in_14(addsub16bit_1_c_in_14));  // open: Q
  Multiplexer #(.Selector_Bits(3), .Bits(16)) multiplexer_1 (
    .sel(ALUOP), .in_0(addsub16bit_1_addition), .in_1(addsub16bit_1_subtraction), .in_2(nand_1_out),
    .in_3(nor_1_out), .in_4(and_1_out), .in_5(or_1_out), .in_6(xor_1_out), .in_7(not_1_out),
    .out({FLAG[1], {2{RESULT[14]}}, RESULT[12:0]}));
  xor xor_2 (xor_2_out, addsub16bit_1_c_out, addsub16bit_1_c_in_14);
  Multiplexer #(.Selector_Bits(3)) multiplexer_2 (
    .sel(ALUOP), .in_0(xor_2_out), .in_1(xor_2_out), .in_2(1'b0), .in_3(1'b0), .in_4(1'b0), .in_5(1'b0),
    .in_6(1'b0), .in_7(1'b0), .out(FLAG[2]));
  Multiplexer #(.Selector_Bits(3)) multiplexer_3 (
    .sel(ALUOP), .in_0(addsub16bit_1_c_out), .in_1(addsub16bit_1_c_out), .in_2(1'b0), .in_3(1'b0),
    .in_4(1'b0), .in_5(1'b0), .in_6(1'b0), .in_7(1'b0), .out(FLAG[3]));
  nor nor_2 (FLAG[0], RESULT[0], RESULT[1], RESULT[2], RESULT[3], RESULT[4], RESULT[5], RESULT[6], RESULT[7], RESULT[8], RESULT[9], RESULT[10], RESULT[11], RESULT[12], RESULT[14], RESULT[14], FLAG[1]);

  assign {RESULT[15], RESULT[13]} = {FLAG[1], RESULT[14]};

  // Notes on the sheet:
  //   A: First input to ALU
  //   B: Second input to ALU
  //   ALUOP: Operation selection input
  //   RESULT: The result of this ALU operation
  //   FLAG: The flags associated with the result of this ALU operation
  //   0. Z (zero)
  //   1. N (negative)
  //   2. V (overflow)
  //   3. C (carry)
endmodule

/* Test case RESULT:
ALUOP A B RESULT

# Test small results
loop(a, 1 << 4)
  loop(b, 1 << 4)
    (0b000) (a) (b) ((a + b) & 0xFFFF)   # ADD
    (0b001) (a) (b) ((a - b) & 0xFFFF)   # SUB
    (0b010) (a) (b) (~(a & b) & 0xFFFF)  # NAND
    (0b011) (a) (b) (~(a | b) & 0xFFFF)  # NOR
    (0b100) (a) (b) (a & b)              # AND
    (0b101) (a) (b) (a | b)              # ORR
    (0b110) (a) (b) (a ^ b)              # XOR
    (0b111) (a) (b) (~a & 0xFFFF)        # NOT
  end loop
end loop


# Test large results
loop(i, 1000)
    let a = random(1 << 16);
    let b = random(1 << 16);

    (0b000) (a) (b) ((a + b) & 0xFFFF)   # ADD
    (0b001) (a) (b) ((a - b) & 0xFFFF)   # SUB
    (0b010) (a) (b) (~(a & b) & 0xFFFF)  # NAND
    (0b011) (a) (b) (~(a | b) & 0xFFFF)  # NOR
    (0b100) (a) (b) (a & b)              # AND
    (0b101) (a) (b) (a | b)              # ORR
    (0b110) (a) (b) (a ^ b)              # XOR
    (0b111) (a) (b) (~a & 0xFFFF)        # NOT
end loop
*/

/* Test case Z:
ALUOP A B Z

declare Z = FLAG & 0b1;

# Test all zero cases
0b000 0 0 1 # AND
0b001 0 0 1 # SUB
0b010 0 0 0 # NAND
0b011 0 0 0 # NOR
0b100 0 0 1 # AND
0b101 0 0 1 # ORR
0b110 0 0 1 # XOR
0b111 0 0 0 # NOT

# Test 1 + (-1) = 0
0b000 1 0xFFFF 1

# Test random inputs
loop(i, 200)
    let a = random(1 << 16);
    let b = random(1 << 16);

    (0b000) (a) (b) (((a + b) & 0xFFFF) = 0)   # ADD
    (0b001) (a) (b) (((a - b) & 0xFFFF) = 0)   # SUB
    (0b010) (a) (b) ((~(a & b) & 0xFFFF) = 0)  # NAND
    (0b011) (a) (b) ((~(a | b) & 0xFFFF) = 0)  # NOR
    (0b100) (a) (b) ((a & b) = 0)              # AND
    (0b101) (a) (b) ((a | b) = 0)              # ORR
    (0b110) (a) (b) ((a ^ b) = 0)              # XOR
    (0b111) (a) (b) ((~a) & 0xFFFF = 0)        # NOT
end loop
*/

/* Test case N:
ALUOP A B N

declare N = (FLAG >> 1) & 0b1;

# Test all zero cases
0b000 0 0 0 # AND
0b001 0 0 0 # SUB
0b010 0 0 1 # NAND
0b011 0 0 1 # NOR
0b100 0 0 0 # AND
0b101 0 0 0 # ORR
0b110 0 0 0 # XOR
0b111 0 0 1 # NOT

# Test 1 + (-1) = 0
0b000 1 0xFFFF 0

# Test random inputs
loop(i, 200)
    let a = random(1 << 16);
    let b = random(1 << 16);

    (0b000) (a) (b) (((a + b) & 0xFFFF) >> 15)   # ADD
    (0b001) (a) (b) (((a - b) & 0xFFFF) >> 15)   # SUB
    (0b010) (a) (b) ((~(a & b) & 0xFFFF) >> 15)  # NAND
    (0b011) (a) (b) ((~(a | b) & 0xFFFF) >> 15)  # NOR
    (0b100) (a) (b) ((a & b) >> 15)              # AND
    (0b101) (a) (b) ((a | b) >> 15)              # ORR
    (0b110) (a) (b) ((a ^ b) >> 15)              # XOR
    (0b111) (a) (b) (((~a) & 0xFFFF) >> 15)        # NOT
end loop
*/

/* Test case V:
ALUOP A B V

declare V = (FLAG >> 2) & 0b1;

# Test zero cases for + / -
0b000 0 0 0
0b001 0 0 0

# 1 + (-1) = 0  ; different input signs = no overflow here!
0b000 1 0xFFFF 0

# 3 - 5 = 3 + (-5) = -2  ; subtraction inverts the second operand sign
0b001 3 5 0

# Some edge cases when subtracting 0x8000
0b001 0x8000 0x8000 0
0b001 0xFFFF 0x8000 0
0b001 0x7FFF 0x8000 1

# Test random inputs
loop(i, 200)
    let a = random(1 << 16);
    let b = random(1 << 16);

    0b000 (a) (b) (((~(a ^ b) & (a ^ (a + b))) >> 15) & 0b1)
    0b001 (a) (b) (((~(a ^ ~b) & (a ^ (a - b))) >> 15) & 0b1)
end loop

# Other operations will not set the overflow flag.
loop(i, 100)
    let a = random(1 << 16);
    let b = random(1 << 16);
    0b010 (a) (b) 0
    0b011 (a) (b) 0
    0b100 (a) (b) 0
    0b101 (a) (b) 0
    0b110 (a) (b) 0
    0b111 (a) (b) 0
end loop
*/

/* Test case C:
ALUOP A B C

declare C = (FLAG >> 3) & 0b1;

# Test 0 + 0
0b000 0 0 0

# (0 - 0) is implemented as 0 + (0xFFFF + 1), so a carry is expected
0b001 0 0 1

# Carry should propagate all the way from the first bit if necessary
0b000 1 0xFFFF 1

# Adding 15 bit values should never carry
loop(i, 100)
    0b000 (random(1 << 15)) (random(1 << 15)) 0
end loop

# Test random inputs
loop(i, 200)
    let a = random(1 << 16);
    let b = random(1 << 16);

    0b000 (a) (b) (((a + b) >> 16) & 0b1)
    0b001 (a) (b) (~((a - b) >> 16) & 0b1)
end loop

# Other operations will not set the C flag.
loop(i, 100)
    let a = random(1 << 16);
    let b = random(1 << 16);
    0b010 (a) (b) 0
    0b011 (a) (b) 0
    0b100 (a) (b) 0
    0b101 (a) (b) 0
    0b110 (a) (b) 0
    0b111 (a) (b) 0
end loop
*/
