// Digital circuit extended-cpu.dig as structural Verilog
module extended_cpu (
  input  CLK,
  output Z,
  output N,
  output C,
  output V
);

  wire control_unit_1_p8, control_unit_1_p9, control_unit_1_p10, control_unit_1_p11, control_unit_1_p12,
       control_unit_1_p13, control_unit_1_p14, control_unit_1_p16, control_unit_1_p17, control_unit_1_p18,
       control_unit_1_p19, myalu_1_p3, myalu_1_p4;
  wire [15:0] decoder_1_out_0, multiplexer_1_out, myalu_1_p1, PC_q, plus_1_s, RAM_d1, RAM_d2, reg_file_1_p12;

  Decoder #(.Selector_Bits(4)) decoder_1 (
    .sel(RAM_d2[11:8]), .out_0(decoder_1_out_0[0]), .out_1(decoder_1_out_0[1]), .out_2(decoder_1_out_0[2]),
    .out_3(decoder_1_out_0[3]), .out_4(decoder_1_out_0[4]), .out_5(decoder_1_out_0[5]),
    .out_6(decoder_1_out_0[6]), .out_7(decoder_1_out_0[7]), .out_8(decoder_1_out_0[8]),
    .out_9(decoder_1_out_0[9]), .out_10(decoder_1_out_0[10]), .out_11(decoder_1_out_0[11]),
    .out_12(decoder_1_out_0[12]), .out_13(decoder_1_out_0[13]), .out_14(decoder_1_out_0[14]),
    .out_15(decoder_1_out_0[15]));
  Multiplexer #(.Bits(16)) multiplexer_1 (
    .sel(control_unit_1_p19), .in_0(reg_file_1_p12), .in_1(decoder_1_out_0), .out(multiplexer_1_out));
  // MYALU myalu_1: pin names not known; wires that end beside it: myalu_1_p1, multiplexer_1_out, myalu_1_p3, myalu_1_p4, {V, C, N, Z}
  Register #(.Bits(16), .isProgramCounter("true")) PC (.D(plus_1_s), .C(CLK), .en(1'b1), .Q(PC_q));
  Add #(.Bits(16)) plus_1 (.a(16'h1), .b(PC_q), .c_i(1'b0), .s(plus_1_s));  // open: c_o
  // Probe on {V, C, N, Z}
  RAMDualAccess #(.AddrBits(16), .isProgramMemory("true"), .Bits(16)) RAM (
    .str(control_unit_1_p16), .C(CLK), .ld(control_unit_1_p17), .A1(myalu_1_p1), .Din1(reg_file_1_p12),
    .A2(PC_q), .D1(RAM_d1), .D2(RAM_d2));
  // control_unit control_unit_1: pin names not known; wires that end beside it: RAM_d1, RAM_d2, myalu_1_p4, Z, N, C, V, control_unit_1_p8, control_unit_1_p9, control_unit_1_p10, control_unit_1_p11, control_unit_1_p12, control_unit_1_p13, control_unit_1_p14, myalu_1_p3, control_unit_1_p16, control_unit_1_p17, control_unit_1_p18, control_unit_1_p19
  // reg_file reg_file_1: pin names not known; wires that end beside it: control_unit_1_p8, control_unit_1_p9, control_unit_1_p10, control_unit_1_p11, control_unit_1_p12, CLK, control_unit_1_p13, control_unit_1_p14, PC_q, control_unit_1_p18, myalu_1_p1, reg_file_1_p12
endmodule

/* Test case CHECK:
# assert these registers can be tested
CLK R1 R2 R3 R4 FL PC

program(0)  # assert program memory exists
init R1=0;  # assert we can initialise R1
init R2=0;  # assert we can initialise R2
init R3=0;  # assert we can initialise R3
init R4=0;  # assert we can initialise R4
init PC=0;  # assert we can initialise PC
init FL=0;  # assert we can initialise FL

0 0 0 0 0 0 0
*/

/* Test case MOVL:
CLK     R1     R2     R3     R4     PC

0        x      x      x      x 0x0000
c   0x0012      x      x      x 0x0001
c   0x0012 0x0034      x      x 0x0002
c   0x0012 0x0034 0x0056      x 0x0003
c   0x0012 0x0034 0x0056 0x0078 0x0004
c   0x0000 0x0034 0x0056 0x0078 0x0005
c   0x0000 0x0001 0x0056 0x0078 0x0006

program(0x0112,0x0234,0x0356,0x0478,0x0100,0x0201)
*/

/* Test case AND/ORR:
CLK     R1     R2     R3     R4     PC

init R2=0x5a96;
init R3=0x5849;
init R4=0xa569;

0        x      x      x      x 0x0000
c   0xFFFF      x      x      x 0x0001
c   0xFFFF 0x5800      x      x 0x0002
c   0xFFFF 0x5800 0x0049      x 0x0003
c   0xFFFF 0x5800 0x0049 0xFFFF 0x0004
c   0x0000 0x5800 0x0049 0xFFFF 0x0005
c   0x0000 0x5800 0x0049 0xFFFF 0x0006

program(0x9124,0x8232,0x8343,0x9410,0x8123,0x9333)
*/

/* Test case ADD/SUB:
CLK     R1     R2     R3     R4     PC

init R1=0x1234;
init R2=0xABCD;
init R3=0xFFFF;

0        x      x      x      x 0x0000
c        x      x      x 0xBE01 0x0001
c        x      x      x 0xBE01 0x0002
c        x      x      x 0xBE02 0x0003
c        x      x      x 0xABCE 0x0004
c        x      x      x 0x0001 0x0005
c        x      x      0 0x0001 0x0006

program(0xa412,0xa440,0xb443,0xb441,0xb442,0xa343)
*/

/* Test case LDR/STR:
CLK     R1     R2     R3     R4     PC

init R1=0x6;
init R4=0x7;

0        x      x      x      x 0x0000
c        x 0x4200      x      x 0x0001
c        x 0x4200      x      x 0x0002
c        x 0x4200 0x0005      x 0x0003
c   0x4410 0x4200 0x0005      x 0x0004
c   0x4410 0x4200 0x0005      x 0x0005
c   0x4410 0x4200 0x0005 0x4200 0x0006
c   0x4410 0x4200 0x0005 0x4200 0x0007

program(0x4200,0x7210,0x4340,0x4130,0x7210,0x4410,0x0001,0x0005)
*/

/* Test case ALU:
CLK     R1     R2     R3     R4   FLAGS     PC

declare FLAGS = FL & 0xF;

init R1=0x1A;
init R2=0xCDFF;
init R3=0x0;

0        x      x      x      x      x 0x0000
c   0x001a 0xcdff      x 0xce19 0x0002 0x0001
c   0x001a 0xcdff      x 0x001a 0x0000 0x0002
c   0x001a 0xcdff      x 0xcdff 0x000A 0x0003
c   0x001a 0xcdff      x 0x3201 0x0000 0x0004
c   0x001a 0xcdff      x 0x0000 0x0001 0x0005
c   0x001a 0xcdff      x 0x0000 0x0001 0x0006
c   0x001a 0xcdff      x 0xcdff 0x0002 0x0007
c   0x001a 0xcdff      x 0xcdff 0x0002 0x0008
c   0x0000 0xcdff      x 0xcdff 0x0001 0x0009
c   0x0000 0x0000      x 0xcdff 0x0001 0x000a

program(0xa412, 0x8421, 0xb423, 0xb432, 0x8413, 0x8431, 0x9412, 0x9012, 0xa100, 0xa230)
*/

/* Test case FLAGS:
CLK     R1     R2     R3     R4   FLAGS     PC

declare FLAGS = FL & 0xF;

init R1=1;
init R2=0xFFFF;
init R3=0x7FFF;
init R4=0x8000;
0        x      x      x      x      x 0x0000
c   0x0001 0xffff 0x7fff 0x8000 0x0001 0x0001
c   0x0001 0xffff 0x7fff 0x8000 0x0009 0x0002
c   0x0001 0xffff 0x7fff 0x8000 0x0009 0x0003
c   0x0001 0xffff 0x7fff 0x8000 0x0000 0x0004
c   0x0001 0xffff 0x7fff 0x8000 0x000A 0x0005
c   0x0001 0xffff 0x7fff 0x8000 0x000A 0x0006
c   0x0001 0xffff 0x7fff 0x8000 0x0002 0x0007
c   0x0001 0xffff 0x7fff 0x8000 0x0002 0x0008
c   0x0001 0xffff 0x7fff 0x8000 0x000c 0x0009
c   0x0001 0xffff 0x7fff 0x8000 0x0008 0x000a
c   0x0001 0xffff 0x7fff 0x8000 0x000c 0x000b
c   0x0001 0xffff 0x7fff 0x8000 0x0006 0x000c

program(0xa000, 0xa012, 0xb011, 0xb012, 0xa022, 0xb021, 0xa034, 0xa041, 0xb041, 0xb031, 0xb043, 0xa013)
*/

/* Test case READ_FLAGS:
CLK     R1     R2     R3     R4     PC

init R1=0x76;
init R4=0xF;
0        x      x      x      x 0x0000
c   0x0076 0x0000      x 0x000f 0x0001
c   0x0076 0x0000      x 0x000f 0x0002
c   0x0076 0x0000 0x0009 0x000f 0x0003

program(0xb211, 0xa370, 0x8334)
*/

/* Test case COND:
CLK     R1     R2     R3     R4     PC

0        x      x      x      x 0x0000
c   0x0000      x      x      x 0x0001
c   0x0000 0x0000      x      x 0x0002
c   0x0000 0x0000 0x0016      x 0x0003
c   0x0000 0x0000 0x0016 0x0001 0x0004
c   0x0000 0x0000 0x0016 0x0001 0x0005
c   0x0000 0x0001 0x0016 0x0001 0x0006
c   0x0000 0x0001 0x0016 0x0001 0x0007
c   0x0000 0x0001 0x0016 0x0001 0x0008
c   0x0000 0x0001 0x0016 0x0001 0x0009
c   0x0000 0x0001 0x0016 0x0001 0x000a
c   0x1337 0x0001 0x0016 0x0001 0x000b
c   0x1337 0x0001 0x0017 0x0001 0x000c
c   0x1337 0x0001 0x0017 0x0001 0x000d
c   0x1337 0x0000 0x0017 0x0001 0x000e
c   0x1337 0x0000 0x0017 0x0001 0x000f
c   0x1337 0x0000 0x0017 0x0001 0x0010
c   0x1337 0x1337 0x0017 0x0001 0x0011
c   0x1337 0x1337 0x0017 0x0001 0x0012
c   0x1337 0x1337 0x0017 0x0001 0x0013
c   0x1337 0x1337 0x0017 0x0001 0x0014
c   0x0051 0x1337 0x0017 0x0001 0x0015

program(0x0100, 0x0200, 0x0316, 0x0401, 0xa000, 0xaa04, 0x9944, 0xb040, 0x4930, 0xb000, 0x4930, 0xa334, 0x7930, 0x4230, 0xb000, 0x7930, 0x4230, 0xb040, 0x0915, 0xb000, 0x0951, 0x0000, 0x1337)
*/

/* Test case GP_PC:
CLK     R1     R2     R3     R4     PC

init R1=0x5;
init R2=0x98;
0        x      x      x      x 0x0000
c   0x0005 0x0098      x      x 0x0001
c   0x0005 0x0098      x      x 0x0002
c   0x0005 0x0002      x      x 0x0003
c   0x0005 0x0002      x      x 0x0005

program(0xa000,0xa000,0xa250,0xa510,0x03ff,0x0000)
*/

/* Test case COND_PC:
CLK     R1     R2     R3     R4     PC

0        x      x      x      x 0x0000
c   0x00FF      x      x      x 0x0001
c   0x00FF 0x00FE      x      x 0x0002
c   0x00FF 0x00FE 0xFFFF      x 0x0003
c   0x00FF 0x00FE 0xFFFF      x 0x0004
c   0x00FF 0x0002 0xFFFF      x 0x0005
c   0x00FF 0x0002 0xFFFF      x 0x0006
c   0x00FF 0x0002 0xFFFF      x 0x0008


program(0x01ff,0x02fe,0xb321,0x0d01,0x0202,0xb433,0xad52,0x0500,0x0112)
*/

/* Test case LOOP:
CLK     R1     R2     R3     R4     PC

init R2=1;
init R4=0x5512;

0        x      x      x      x 0x0000
c        x      1 0x5511 0x5512 0x0001
c   0x0000      1 0x5511 0x5510 0x0002
c   0x0001      1 0x5511 0x5510 0x0003
c   0x0001      1 0x5511 0x5510 0x0004
c   0x0001      1 0x5511 0x5510 0x0005

c   0x0001      1 0x5511 0x5510 0x0000
c   0x0001      1 0x550F 0x5510 0x0001
c   0x0001      1 0x550F 0x5500 0x0002
c   0x0002      1 0x550F 0x5500 0x0003
c   0x0002      1 0x550F 0x5500 0x0004
c   0x0002      1 0x550F 0x5500 0x0005

c   0x0002      1 0x550F 0x5500 0x0000
c   0x0002      1 0x54FF 0x5500 0x0001
c   0x0002      1 0x54FF 0x5400 0x0002
c   0x0003      1 0x54FF 0x5400 0x0003
c   0x0003      1 0x54FF 0x5400 0x0004
c   0x0003      1 0x54FF 0x5400 0x0005

c   0x0003      1 0x54FF 0x5400 0x0000
c   0x0003      1 0x53FF 0x5400 0x0001
c   0x0003      1 0x53FF 0x5000 0x0002
c   0x0004      1 0x53FF 0x5000 0x0003
c   0x0004      1 0x53FF 0x5000 0x0004
c   0x0004      1 0x53FF 0x5000 0x0005

c   0x0004      1 0x53FF 0x5000 0x0000
c   0x0004      1 0x4FFF 0x5000 0x0001
c   0x0004      1 0x4FFF 0x4000 0x0002
c   0x0005      1 0x4FFF 0x4000 0x0003
c   0x0005      1 0x4FFF 0x4000 0x0004
c   0x0005      1 0x4FFF 0x4000 0x0005

c   0x0005      1 0x4FFF 0x4000 0x0000
c   0x0005      1 0x3FFF 0x4000 0x0001
c   0x0005      1 0x3FFF 0x0000 0x0002
c   0x0006      1 0x3FFF 0x0000 0x0003
c   0x0006      1 0x3FFF 0x0000 0x0004
c   0x0006      1 0x3FFF 0x0000 0x0006
c   0x0006      1 0x3FFF 0x0006 0x0007
c   0x0000      1 0x3FFF 0x0006 0x0008
c   0x0000      1 0x3FFF 0x0006 0x0009
c   0x0000      1 0x3FFF 0x0006 0x000A
c   0x0000      1 0x3FFF 0x0006 0x000B
c   0x0000      1 0x3FFF 0x0006 0x0000
c   0x0000      1 0x0005 0x0006 0x0001
c   0x0000      1 0x0005 0x0004 0x0002
c   0x0001      1 0x0005 0x0004 0x0003
c   0x0001      1 0x0005 0x0004 0x0004
c   0x0001      1 0x0005 0x0004 0x0005
c   0x0001      1 0x0005 0x0004 0x0000
c   0x0001      1 0x0003 0x0004 0x0001
c   0x0001      1 0x0003 0x0000 0x0002
c   0x0002      1 0x0003 0x0000 0x0003
c   0x0002      1 0x0003 0x0000 0x0004
c   0x0002      1 0x0003 0x0000 0x0006
c   0x0002      1 0x0003 0x0002 0x0007
c   0x0000      1 0x0003 0x0002 0x0008
c   0x0000      1 0x0003 0x0002 0x0009
c   0x0000      1 0x0003 0x0002 0x000A
c   0x0000      1 0x0003 0x0002 0x000B
c   0x0000      1 0x0003 0x0002 0x0000
c   0x0000      1 0x0001 0x0002 0x0001
c   0x0000      1 0x0001 0x0000 0x0002
c   0x0001      1 0x0001 0x0000 0x0003
c   0x0001      1 0x0001 0x0000 0x0004
c   0x0001      1 0x0001 0x0000 0x0006
c   0x0001      1 0x0001 0x0001 0x0007
c   0x0000      1 0x0001 0x0001 0x0008
c   0x0000      1 0x0001 0x0001 0x0009
c   0x0000      1 0x0001 0x0001 0x00FF


program(0xb342,0x8443,0xa112,0xb040,0x0d06,0x0500,0x9401,0x0100,0xb024,0x0dff,0x8110,0x0d00)
*/

/* Test case REC:
CLK     R1     R2     R3     R4     PC

0        x      x      x      x 0x0000
c        x      x      x 0x0000 0x0001
c   0x0020      x      x 0x0000 0x0002
c   0x0020 0x0008      x 0x0000 0x0003
c   0x0020 0x0008 0x0001 0x0000 0x0004
c   0x0021 0x0008 0x0001 0x0000 0x0005
c   0x0021 0x0008 0x0001 0xffff 0x0006
c   0x0021 0x0008 0x001f 0xffff 0x0007
c   0x0021 0x0008 0x001f 0xffff 0x0008
c   0x0021 0x0008 0x001f 0xffff 0x0009
c   0x0021 0x0008 0x001f 0xffff 0x000a
c   0x0021 0x0008 0x0001 0xffff 0x000b
c   0x0021 0x0008 0x0001 0xfffe 0x000c
c   0x0021 0x0008 0x0001 0xfffe 0x000d
c   0x000f 0x0008 0x0001 0xfffe 0x000e
c   0x000f 0x0008 0x0001 0xfffd 0x000f
c   0x000f 0x0008 0x0001 0xfffd 0x0010
c   0x000f 0x0007 0x0001 0xfffd 0x0011
c   0xfffe 0x0007 0x0001 0xfffd 0x0012
c   0x0021 0x0007 0x0001 0xfffd 0x0013
c   0x0022 0x0007 0x0001 0xfffd 0x0014
c   0x0022 0x0007 0x0001 0xfffc 0x0015
c   0x0022 0x0007 0x0018 0xfffc 0x0016
c   0x0022 0x0007 0x0018 0xfffc 0x0017
c   0x0022 0x0007 0x0018 0xfffc 0x0008
c   0x0022 0x0007 0x0018 0xfffc 0x0009
c   0x0022 0x0007 0x0018 0xfffc 0x000a
c   0x0022 0x0007 0x0001 0xfffc 0x000b
c   0x0022 0x0007 0x0001 0xfffb 0x000c
c   0x0022 0x0007 0x0001 0xfffb 0x000d
c   0x0004 0x0007 0x0001 0xfffb 0x000e
c   0x0004 0x0007 0x0001 0xfffa 0x000f
c   0x0004 0x0007 0x0001 0xfffa 0x0010
c   0x0004 0x0006 0x0001 0xfffa 0x0011
c   0xfffb 0x0006 0x0001 0xfffa 0x0012
c   0x0022 0x0006 0x0001 0xfffa 0x0013
c   0x0023 0x0006 0x0001 0xfffa 0x0014
c   0x0023 0x0006 0x0001 0xfff9 0x0015
c   0x0023 0x0006 0x0018 0xfff9 0x0016
c   0x0023 0x0006 0x0018 0xfff9 0x0017
c   0x0023 0x0006 0x0018 0xfff9 0x0008
c   0x0023 0x0006 0x0018 0xfff9 0x0009
c   0x0023 0x0006 0x0018 0xfff9 0x000a
c   0x0023 0x0006 0x0001 0xfff9 0x000b
c   0x0023 0x0006 0x0001 0xfff8 0x000c
c   0x0023 0x0006 0x0001 0xfff8 0x000d
c   0x0005 0x0006 0x0001 0xfff8 0x000e
c   0x0005 0x0006 0x0001 0xfff7 0x000f
c   0x0005 0x0006 0x0001 0xfff7 0x0010
c   0x0005 0x0005 0x0001 0xfff7 0x0011
c   0xfff8 0x0005 0x0001 0xfff7 0x0012
c   0x0023 0x0005 0x0001 0xfff7 0x0013
c   0x0024 0x0005 0x0001 0xfff7 0x0014
c   0x0024 0x0005 0x0001 0xfff6 0x0015
c   0x0024 0x0005 0x0018 0xfff6 0x0016
c   0x0024 0x0005 0x0018 0xfff6 0x0017
c   0x0024 0x0005 0x0018 0xfff6 0x0008
c   0x0024 0x0005 0x0018 0xfff6 0x0009
c   0x0024 0x0005 0x0018 0xfff6 0x000a
c   0x0024 0x0005 0x0001 0xfff6 0x000b
c   0x0024 0x0005 0x0001 0xfff5 0x000c
c   0x0024 0x0005 0x0001 0xfff5 0x000d
c   0x0006 0x0005 0x0001 0xfff5 0x000e
c   0x0006 0x0005 0x0001 0xfff4 0x000f
c   0x0006 0x0005 0x0001 0xfff4 0x0010
c   0x0006 0x0004 0x0001 0xfff4 0x0011
c   0xfff5 0x0004 0x0001 0xfff4 0x0012
c   0x0024 0x0004 0x0001 0xfff4 0x0013
c   0x0025 0x0004 0x0001 0xfff4 0x0014
c   0x0025 0x0004 0x0001 0xfff3 0x0015
c   0x0025 0x0004 0x0018 0xfff3 0x0016
c   0x0025 0x0004 0x0018 0xfff3 0x0017
c   0x0025 0x0004 0x0018 0xfff3 0x0008
c   0x0025 0x0004 0x0018 0xfff3 0x0009
c   0x0025 0x0004 0x0018 0xfff3 0x000a
c   0x0025 0x0004 0x0001 0xfff3 0x000b
c   0x0025 0x0004 0x0001 0xfff2 0x000c
c   0x0025 0x0004 0x0001 0xfff2 0x000d
c   0x0007 0x0004 0x0001 0xfff2 0x000e
c   0x0007 0x0004 0x0001 0xfff1 0x000f
c   0x0007 0x0004 0x0001 0xfff1 0x0010
c   0x0007 0x0003 0x0001 0xfff1 0x0011
c   0xfff2 0x0003 0x0001 0xfff1 0x0012
c   0x0025 0x0003 0x0001 0xfff1 0x0013
c   0x0026 0x0003 0x0001 0xfff1 0x0014
c   0x0026 0x0003 0x0001 0xfff0 0x0015
c   0x0026 0x0003 0x0018 0xfff0 0x0016
c   0x0026 0x0003 0x0018 0xfff0 0x0017
c   0x0026 0x0003 0x0018 0xfff0 0x0008
c   0x0026 0x0003 0x0018 0xfff0 0x0009
c   0x0026 0x0003 0x0018 0xfff0 0x000a
c   0x0026 0x0003 0x0001 0xfff0 0x000b
c   0x0026 0x0003 0x0001 0xffef 0x000c
c   0x0026 0x0003 0x0001 0xffef 0x000d
c   0x0008 0x0003 0x0001 0xffef 0x000e
c   0x0008 0x0003 0x0001 0xffee 0x000f
c   0x0008 0x0003 0x0001 0xffee 0x0010
c   0x0008 0x0002 0x0001 0xffee 0x0011
c   0xffef 0x0002 0x0001 0xffee 0x0012
c   0x0026 0x0002 0x0001 0xffee 0x0013
c   0x0027 0x0002 0x0001 0xffee 0x0014
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*/

/* Test case FIB:
CLK     R1     R2     R3     R4   FLAGS     PC

declare FLAGS = FL & 0xF;

0        x      x      x      x      x 0x0000
c   0x0001      x      x      x      x 0x0001
c   0x0001 0x0000      x      x      x 0x0002
c   0x0001 0x0000 0x0019      x      x 0x0003
c   0x0001 0x0000 0x0019      x 0x0008 0x0004
c   0x0001 0x0000 0x0019      x 0x0008 0x0005
c   0x0001 0x0000 0x0019 0x0001 0x0000 0x0006
c   0x0000 0x0000 0x0019 0x0001 0x0001 0x0007
c   0x0000 0x0001 0x0019 0x0001 0x0000 0x0008
c   0x0000 0x0001 0x0019 0x0001 0x0000 0x0009
c   0x0000 0x0001 0x0018 0x0001 0x0008 0x000a
c   0x0000 0x0001 0x0018 0x0001 0x0008 0x0003
c   0x0000 0x0001 0x0018 0x0001 0x0008 0x0004
c   0x0000 0x0001 0x0018 0x0001 0x0008 0x0005
c   0x0000 0x0001 0x0018 0x0001 0x0000 0x0006
c   0x0001 0x0001 0x0018 0x0001 0x0000 0x0007
c   0x0001 0x0001 0x0018 0x0001 0x0000 0x0008
c   0x0001 0x0001 0x0018 0x0001 0x0000 0x0009
c   0x0001 0x0001 0x0017 0x0001 0x0008 0x000a
c   0x0001 0x0001 0x0017 0x0001 0x0008 0x0003
c   0x0001 0x0001 0x0017 0x0001 0x0008 0x0004
c   0x0001 0x0001 0x0017 0x0001 0x0008 0x0005
c   0x0001 0x0001 0x0017 0x0002 0x0000 0x0006
c   0x0001 0x0001 0x0017 0x0002 0x0000 0x0007
c   0x0001 0x0002 0x0017 0x0002 0x0000 0x0008
c   0x0001 0x0002 0x0017 0x0001 0x0000 0x0009
c   0x0001 0x0002 0x0016 0x0001 0x0008 0x000a
c   0x0001 0x0002 0x0016 0x0001 0x0008 0x0003
c   0x0001 0x0002 0x0016 0x0001 0x0008 0x0004
c   0x0001 0x0002 0x0016 0x0001 0x0008 0x0005
c   0x0001 0x0002 0x0016 0x0003 0x0000 0x0006
c   0x0002 0x0002 0x0016 0x0003 0x0000 0x0007
c   0x0002 0x0003 0x0016 0x0003 0x0000 0x0008
c   0x0002 0x0003 0x0016 0x0001 0x0000 0x0009
c   0x0002 0x0003 0x0015 0x0001 0x0008 0x000a
c   0x0002 0x0003 0x0015 0x0001 0x0008 0x0003
c   0x0002 0x0003 0x0015 0x0001 0x0008 0x0004
c   0x0002 0x0003 0x0015 0x0001 0x0008 0x0005
c   0x0002 0x0003 0x0015 0x0005 0x0000 0x0006
c   0x0003 0x0003 0x0015 0x0005 0x0000 0x0007
c   0x0003 0x0005 0x0015 0x0005 0x0000 0x0008
c   0x0003 0x0005 0x0015 0x0001 0x0000 0x0009
c   0x0003 0x0005 0x0014 0x0001 0x0008 0x000a
c   0x0003 0x0005 0x0014 0x0001 0x0008 0x0003
c   0x0003 0x0005 0x0014 0x0001 0x0008 0x0004
c   0x0003 0x0005 0x0014 0x0001 0x0008 0x0005
c   0x0003 0x0005 0x0014 0x0008 0x0000 0x0006
c   0x0005 0x0005 0x0014 0x0008 0x0000 0x0007
c   0x0005 0x0008 0x0014 0x0008 0x0000 0x0008
c   0x0005 0x0008 0x0014 0x0001 0x0000 0x0009
c   0x0005 0x0008 0x0013 0x0001 0x0008 0x000a
c   0x0005 0x0008 0x0013 0x0001 0x0008 0x0003
c   0x0005 0x0008 0x0013 0x0001 0x0008 0x0004
c   0x0005 0x0008 0x0013 0x0001 0x0008 0x0005
c   0x0005 0x0008 0x0013 0x000d 0x0000 0x0006
c   0x0008 0x0008 0x0013 0x000d 0x0000 0x0007
c   0x0008 0x000d 0x0013 0x000d 0x0000 0x0008
c   0x0008 0x000d 0x0013 0x0001 0x0000 0x0009
c   0x0008 0x000d 0x0012 0x0001 0x0008 0x000a
c   0x0008 0x000d 0x0012 0x0001 0x0008 0x0003
c   0x0008 0x000d 0x0012 0x0001 0x0008 0x0004
c   0x0008 0x000d 0x0012 0x0001 0x0008 0x0005
c   0x0008 0x000d 0x0012 0x0015 0x0000 0x0006
c   0x000d 0x000d 0x0012 0x0015 0x0000 0x0007
c   0x000d 0x0015 0x0012 0x0015 0x0000 0x0008
c   0x000d 0x0015 0x0012 0x0001 0x0000 0x0009
c   0x000d 0x0015 0x0011 0x0001 0x0008 0x000a
c   0x000d 0x0015 0x0011 0x0001 0x0008 0x0003
c   0x000d 0x0015 0x0011 0x0001 0x0008 0x0004
c   0x000d 0x0015 0x0011 0x0001 0x0008 0x0005
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*/

/* Test case SETH:
CLK     R1     R2     R3     R4     PC

init R1=0xAD;
init R2=0x0D;
init R3=0xEF;
init R4=0xAD;
0        x      x      x      x 0x0000
c   0xdead 0x000d 0x00ef 0x00ad 0x0001
c   0xdead 0xf00d 0x00ef 0x00ad 0x0002
c   0xdead 0xf00d 0xbeef 0x00ad 0x0003
c   0xdead 0xf00d 0xbeef 0x0bad 0x0004

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*/

/* Test case SETH_PC:
CLK     R1     R2     R3     R4     PC

0        x      x      x      x 0x0000
c   0x0001      x      x      x 0x0001
c   0x0001 0x0002      x      x 0x0002
c   0x0001 0x0002 0x0003      x 0x0003
c   0x0001 0x0002 0x0006      x 0x0004
c   0x0001 0x0002 0x0006      x 0x0104
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*/
