// Digital circuit reg_file.dig as structural Verilog
module reg_file (
  input  [2:0] WS,
  input  [2:0] RS1,
  input  [2:0] RS2,
  input  WE,
  input  [15:0] IN,
  input  clk,
  input  [3:0] _16FLAG,
  input  FLEN,
  input  [15:0] PC,
  output [15:0] OUT1,
  output [15:0] OUT2
);

  wire and_1_out, and_2_out, and_3_out, and_4_out, decoder_1_out_1, decoder_1_out_2, decoder_1_out_3,
       decoder_1_out_4;
  wire [15:0] FL_q, notconnected_1_out, notconnected_2_out, R1_q, R2_q, R3_q, R4_q;

  Decoder #(.Selector_Bits(3)) decoder_1 (
    .sel(WS), .out_1(decoder_1_out_1), .out_2(decoder_1_out_2), .out_3(decoder_1_out_3),
    .out_4(decoder_1_out_4));  // open: out_0, out_5, out_6, out_7
  and and_1 (and_1_out, WE, decoder_1_out_1);
  and and_2 (and_2_out, WE, decoder_1_out_2);
  and and_3 (and_3_out, WE, decoder_1_out_3);
  and and_4 (and_4_out, WE, decoder_1_out_4);
  Register #(.Bits(16)) R1 (.D(IN), .C(clk), .en(and_1_out), .Q(R1_q));
  Register #(.Bits(16)) R2 (.D(IN), .C(clk), .en(and_2_out), .Q(R2_q));
  Register #(.Bits(16)) R3 (.D(IN), .C(clk), .en(and_3_out), .Q(R3_q));
  Register #(.Bits(16)) R4 (.D(IN), .C(clk), .en(and_4_out), .Q(R4_q));
  Register #(.Bits(16)) FL (.D({{12{1'b0}}, _16FLAG}), .C(clk), .en(FLEN), .Q(FL_q));
  // NotConnected on notconnected_1_out
  // NotConnected on notconnected_2_out
  Multiplexer #(.Selector_Bits(3), .Bits(16)) multiplexer_1 (
    .sel(RS1), .in_0({16{1'b0}}), .in_1(R1_q), .in_2(R2_q), .in_3(R3_q), .in_4(R4_q), .in_5(PC),
    .in_6(notconnected_1_out), .in_7(FL_q), .out(OUT1));
  Multiplexer #(.Selector_Bits(3), .Bits(16)) multiplexer_2 (
    .sel(RS2), .in_0({16{1'b0}}), .in_1(R1_q), .in_2(R2_q), .in_3(R3_q), .in_4(R4_q), .in_5(PC),
    .in_6(notconnected_2_out), .in_7(FL_q), .out(OUT2));

  // Notes on the sheet:
  //   WS: The index of the register which should save the value on IN on the next clock cycle (if WE is high).
  //   RS1: The index of the register which should output its value to OUT1.
  //   RS2: The index of the register which should output its value to OUT2.
  //   WE: Whether the register selected by WS should save the value from IN on the next cycle.
  //   IN: The value to be saved into the register specified by WS if WE is high,
  //   OUT1: The value in the register specified by RS1.
  //   OUT2: The value in the register specified by RS2.
endmodule
